// Digital circuit cpu.dig as structural Verilog
module cpu (
  input  clk,
  input  [31:0] in_2,
  input  [31:0] in_3
);

  wire button_1_out, u_Control_Uint_ex_en, u_Control_Uint_expc_en, u_Control_Uint_id_en,
       u_Control_Uint_imm_en, u_Control_Uint_jump_en, u_Control_Uint_l_or_s, u_Control_Uint_mem_en,
       u_Control_Uint_pc_en, u_Control_Uint_wb_en, u_id_reg1_read_o, u_id_reg2_read_o;
  wire [1:0] u_Control_Uint_wb_ctrl;
  wire [2:0] u_id_aluop_o;
  wire [4:0] u_id_reg1_addr_o, u_id_reg2_addr_o, u_id_wd_o;
  wire [6:0] u_id_alusel_o;
  wire [31:0] u_ex_alu_result, u_id_imm_o, u_id_reg1_o, u_id_reg2_o, u_pc_pc, u_pc_pc_plus_4,
       u_regfile_rdata1, u_regfile_rdata2, u_WB_wb_data;

  Button #(.activeLow("true")) button_1 (.out(button_1_out));
  Control_Uint #(.applicationType("IVERILOG"), .CodeFile("D:\\CPU\\design\\Control_Unit.v")) u_Control_Uint (
    .clk(clk), .rst(button_1_out), .ALUSEL(u_id_alusel_o), .PC_en(u_Control_Uint_pc_en),
    .ID_en(u_Control_Uint_id_en), .EX_en(u_Control_Uint_ex_en), .MEM_en(u_Control_Uint_mem_en),
    .WB_en(u_Control_Uint_wb_en), .Jump_en(u_Control_Uint_jump_en), .imm_en(u_Control_Uint_imm_en),
    .EXPC_en(u_Control_Uint_expc_en), .L_or_S(u_Control_Uint_l_or_s), .WB_Ctrl(u_Control_Uint_wb_ctrl));
  LED led_1 (.in(u_Control_Uint_mem_en));
  LED led_2 (.in(u_Control_Uint_l_or_s));
  pc #(.applicationType("IVERILOG")) u_pc (
    .rst(button_1_out), .pc_en(u_Control_Uint_pc_en), .branch(u_ex_alu_result),
    .branch_en(u_Control_Uint_jump_en), .pc(u_pc_pc), .pc_plus_4(u_pc_pc_plus_4));
  id #(.applicationType("IVERILOG")) u_id (
    .rst(button_1_out), .inst_i(in_3), .reg1_data_i(u_regfile_rdata1), .reg2_data_i(u_regfile_rdata2),
    .id_en(u_Control_Uint_id_en), .reg1_read_o(u_id_reg1_read_o), .reg2_read_o(u_id_reg2_read_o),
    .reg1_addr_o(u_id_reg1_addr_o), .reg2_addr_o(u_id_reg2_addr_o), .aluop_o(u_id_aluop_o),
    .alusel_o(u_id_alusel_o), .reg1_o(u_id_reg1_o), .reg2_o(u_id_reg2_o), .wd_o(u_id_wd_o), .imm_o(u_id_imm_o));
  ex #(.applicationType("IVERILOG"), .CodeFile("D:\\CPU\\design\\ex.v")) u_ex (
    .rst(button_1_out), .en(u_Control_Uint_ex_en), .pc_en(u_Control_Uint_expc_en),
    .imm_en(u_Control_Uint_imm_en), .pc(u_pc_pc), .reg_1(u_id_reg1_o), .reg_2(u_id_reg2_o), .imm(u_id_imm_o),
    .aluop(u_id_aluop_o), .alu_result(u_ex_alu_result));
  WB #(.applicationType("IVERILOG"), .CodeFile("D:\\CPU\\design\\WB.v")) u_WB (
    .RAM_Data(in_2), .PC_Plus4(u_pc_pc_plus_4), .EX_Data(u_ex_alu_result), .WB_Ctrl(u_Control_Uint_wb_ctrl),
    .WB_Data(u_WB_wb_data));
  regfile #(.applicationType("IVERILOG")) u_regfile (
    .clk(clk), .rst(button_1_out), .we(u_Control_Uint_wb_en), .waddr(u_id_wd_o), .wdata(u_WB_wb_data),
    .re1(u_id_reg1_read_o), .raddr1(u_id_reg1_addr_o), .re2(u_id_reg2_read_o), .raddr2(u_id_reg2_addr_o),
    .rdata1(u_regfile_rdata1), .rdata2(u_regfile_rdata2));

  // Notes on the sheet:
  //   clk: Hz: 2
endmodule

/* Code of pc:
// global define
`define RstEnable 1'b1
`define RstDisable 1'b0
`define WriteEnable 1'b1
`define WriteDisable 1'b0
`define ReadEnable 1'b1
`define ReadDisable 1'b0
`define AluOpBus    6:0 //the width of translation aluop_o
`define AluSelBus   2:0 //the width of translation alusel_o
`define InstValid   1'b0 //vaild operator
`define InstInvalid 1'b1 //invaild operator
`define True_v      1'b1//meaning true
`define False_v     1'b0//meaning false
`define ChipDisable 1'b0//chip enable
`define ChipEnable  1'b1//chip ban

//opcode
`define EXE_R_OP          7'b0110011//R type opcode
`define EXE_I_OP          7'b0010011//I type opcode
`define EXE_B_OP          7'b1100011//B type opcode

//special 4 instructions opcode
`define EXE_LW        7'b0000011
`define EXE_SW        7'b0100011
`define EXE_JAL       7'b1101111
`define EXE_JALR      7'b1100111

//func3
`define EXE_OR            3'b110
`define EXE_AND           3'b111
`define EXE_ORI           3'b110
`define EXE_ADDI          3'b000
`define EXE_ANDI          3'b111
`define EXE_BEQ           3'b000
`define EXE_BNE           3'b001 
`define EXE_BLT           3'b100
`define EXE_BGE           3'b101
`define EXE_BLTU          3'b110
`define EXE_BGEU          3'b111
`define EXE_XOR           3'b100
`define EXE_XORI          3'b100

// func7
`define EXE_ADD           7'b0000000 
`define EXE_SUB           7'b0100000

//AluSel
`define EXE_RES_NOP                      7'b0000000
`define EXE_RES_R                        7'b0000101
`define EXE_RES_I                        7'b0100101
`define EXE_RES_LW                       7'b0101001
`define EXE_RES_SW                       7'b0111001
`define EXE_RES_B                        7'b1100010
`define EXE_RES_NB                       7'b0000000
`define EXE_RES_JAL                      7'b1100011
`define EXE_RES_JALR                     7'b1100111

//Aluop
//`define EXE_OR_OP 
//`define EXE_ADD_OP 
`define EXE_NOP_OP        3'b000//0
`define EXE_OR_OP         3'b001//1
`define EXE_AND_OP        3'b010//2
`define EXE_XOR_OP        3'b011//3
                          
`define EXE_ADD_OP        3'b100//4
`define EXE_SUB_OP        3'b101//5
                          
`define EXE_LW_OP         3'b101//4
`define EXE_SW_OP         3'b101//4
                          
`define EXE_BEQ_OP        3'b101//4
`define EXE_BNE_OP        3'b101//4
`define EXE_BLT_OP        3'b101//4
`define EXE_BGE_OP        3'b101//4
`define EXE_BLTU_OP       3'b101//4
`define EXE_BGEU_OP       3'b101//4
                          
`define EXE_JAL_OP        3'b101//4
`define EXE_JALR_OP       3'b101//4

//transer define
`define Branch      1'b1//transer 
`define NotBranch   1'b0//not transfer

//instruction memory about rom
`define ZeroWord    32'h00000000
`define InstAddrBus 31:0  //address
`define InstBus     31:0 //Data
`define InstMemNum  131071 //rom fact size 128K
`define InstMemNumLog2 17     //the real width of rom


//************************ reg total define
`define RegAddrBus  4:0   //regfile addr width
`define RegBus      31:0  //regfile data width
`define RegWidth    32    //in common use reg width
`define DoubleRegwidth 64 // double reg width
`define DoubleRegBus  63:0 //double data width
`define RegNum        32 //the num of reg
`define RegNumLog2    5 //the num of common reg
`define NOPRegAddr    5'b00000

module pc(
    input   wire                                        rst,
    input   wire                                        pc_en,
    input   wire[`InstAddrBus]                          branch,//transer address
    input   wire                                        branch_en,//jump enable
    
    output  reg  [`RegBus]                                pc,//[31:0]
    output  wire  [`RegBus]                             pc_plus_4
);
//************************* main code ************************* //
assign pc_plus_4=pc+'d4;

always@(posedge pc_en or posedge rst)begin
    if(rst==`RstEnable)begin
        pc<=32'h00000000;       //rst to clear out the data
    end
    else if (pc_en)begin         // when pc_en is high for one period,the pc value will upgrade
        if(branch_en==`Branch)begin  
            pc<=branch;
        end
        else begin
            pc<=pc+4;
        end
    end
    else begin
        pc <= pc;
    end
end
//************************************************************ //
endmodule
*/

/* Code of id:
// global define
`define RstEnable 1'b1
`define RstDisable 1'b0
`define WriteEnable 1'b1
`define WriteDisable 1'b0
`define ReadEnable 1'b1
`define ReadDisable 1'b0
`define AluOpBus    2:0 //the width of translation aluop_o
`define AluSelBus   6:0 //the width of translation alusel_o
`define InstValid   1'b0 //vaild operator
`define InstInvalid 1'b1 //invaild operator
`define True_v      1'b1//meaning true
`define False_v     1'b0//meaning false
`define ChipDisable 1'b0//chip enable
`define ChipEnable  1'b1//chip ban

//opcode
`define EXE_R_OP          7'b0110011//R type opcode
`define EXE_I_OP          7'b0010011//I type opcode
`define EXE_B_OP          7'b1100011//B type opcode

//special 4 instructions opcode
`define EXE_LW        7'b0000011
`define EXE_SW        7'b0100011
`define EXE_JAL       7'b1101111
`define EXE_JALR      7'b1100111

//func3
`define EXE_OR            3'b110
`define EXE_AND           3'b111
`define EXE_ORI           3'b110
`define EXE_ADDI          3'b000
`define EXE_ANDI          3'b111
`define EXE_BEQ           3'b000
`define EXE_BNE           3'b001 
`define EXE_BLT           3'b100
`define EXE_BGE           3'b101
`define EXE_BLTU          3'b110
`define EXE_BGEU          3'b111
`define EXE_XOR           3'b100
`define EXE_XORI          3'b100

// func7
`define EXE_ADD           7'b0000000 
`define EXE_SUB           7'b0100000

//AluSel
`define EXE_RES_NOP                      7'b0000000
`define EXE_RES_R                        7'b0000101
`define EXE_RES_I                        7'b0100101
`define EXE_RES_LW                       7'b0101001
`define EXE_RES_SW                       7'b0111001
`define EXE_RES_B                        7'b1100010
`define EXE_RES_NB                       7'b0000000
`define EXE_RES_JAL                      7'b1100011
`define EXE_RES_JALR                     7'b1100111

//Aluop
//`define EXE_OR_OP 
//`define EXE_ADD_OP 
`define EXE_NOP_OP        3'b000//0
`define EXE_OR_OP         3'b001//1
`define EXE_AND_OP        3'b010//2
`define EXE_XOR_OP        3'b011//3
                          
`define EXE_ADD_OP        3'b100//4
`define EXE_SUB_OP        3'b101//5
                          
`define EXE_LW_OP         3'b101//4
`define EXE_SW_OP         3'b101//4
                          
`define EXE_BEQ_OP        3'b101//4
`define EXE_BNE_OP        3'b101//4
`define EXE_BLT_OP        3'b101//4
`define EXE_BGE_OP        3'b101//4
`define EXE_BLTU_OP       3'b101//4
`define EXE_BGEU_OP       3'b101//4
                          
`define EXE_JAL_OP        3'b101//4
`define EXE_JALR_OP       3'b101//4

//transer define
`define Branch      1'b1//transer 
`define NotBranch   1'b0//not transfer

//instruction memory about rom
`define ZeroWord    32'h00000000
`define InstAddrBus 31:0  //address
`define InstBus     31:0 //Data
`define InstMemNum  131071 //rom fact size 128K
`define InstMemNumLog2 17     //the real width of rom


//************************ reg total define
`define RegAddrBus  4:0   //regfile addr width
`define RegBus      31:0  //regfile data width
`define RegWidth    32    //in common use reg width
`define DoubleRegwidth 64 // double reg width
`define DoubleRegBus  63:0 //double data width
`define RegNum        32 //the num of reg
`define RegNumLog2    5 //the num of common reg
`define NOPRegAddr    5'b00000

module id(
    input wire                  rst,
    input wire  [`InstBus]      inst_i,   
    //read the value of Regfile
    input wire  [`RegBus]       reg1_data_i,//the data from reg1
    input wire  [`RegBus]       reg2_data_i,//the data from reg2

    input wire                  id_en,      //the enable signal come from if_id module
    //output to Regfile
    output reg                  reg1_read_o,
    output reg                  reg2_read_o,
    output reg  [`RegAddrBus]   reg1_addr_o,
    output reg  [`RegAddrBus]   reg2_addr_o,
    //output to execute stage
    output reg  [`AluOpBus]     aluop_o,    // the specifical operate signal
    output reg  [`AluSelBus]    alusel_o,   // the operation type
    output reg  [`RegBus]       reg1_o,
    output reg  [`RegBus]       reg2_o,
    output reg  [4:0]           wd_o,
    output reg  [`RegBus]       imm_o
);

//getting the operation code and func3 and func7
wire [6:0]         op1=inst_i[6:0];          //opcode
wire [2:0]         op2=inst_i[14:12];        //func3 or part of imm
wire [6:0]         op3=inst_i[31:25];        //func7

//conserve the instruction needed imm
    //output to execute stage
reg  [`AluOpBus]     aluop;    // the specifical operate signal
reg  [`AluSelBus]    alusel;   // the operation type
reg  [`RegBus]       reg1;
reg  [`RegBus]       reg2;
reg  [4:0]           wd;
reg  [`RegBus]       imm;







//******************************************************** //
//************************main code*********************** //
//******************************************************** //
//stage one : decode
always @(*) begin
if(rst ==`RstEnable) begin
        aluop <= `EXE_NOP_OP  ;
        alusel <= `EXE_RES_NOP;     
        wd <= `NOPRegAddr;
        reg1_read_o <= 1'b0;
        reg2_read_o <= 1'b0;
        reg1_addr_o <= `NOPRegAddr;
        reg2_addr_o <= `NOPRegAddr;
        imm <= 32'h0;
end 
else begin
        aluop <= `EXE_NOP_OP  ;
        alusel <= `EXE_RES_NOP;
        wd <= `NOPRegAddr;
        reg1_read_o<= 1'b0;
        reg2_read_o<= 1'b0;
        reg1_addr_o<= inst_i[19:15];//default read from regfile pole one
        reg2_addr_o <= inst_i[25:21];//default read from regfile pole two
        imm <= `ZeroWord;       
    case (op1)
        `EXE_R_OP:   begin   //R type opcode
                     case (op2)
                     3'b000:begin
                                case(op3)
                                
                                `EXE_ADD:begin
                                 aluop<= `EXE_ADD_OP;
                                 alusel<=`EXE_RES_R ;
                                 reg1_read_o<=1'b1;
                                 reg2_read_o<=1'b1;
                                 imm<=32'h0;
                                 wd<=inst_i[11:7];
                                 end
                                 
                                `EXE_SUB:begin
                                 aluop <= `EXE_SUB_OP;
                                 alusel<=`EXE_RES_R;
                                 reg1_read_o<=1'b1;
                                 reg2_read_o<=1'b1;
                                 imm<=32'h0 ;                                          
                                 wd<=inst_i[11:7];
                                 end
                                 default:begin
                                 end
                                 endcase//op3
                      end//3'b000
                      
                     `EXE_OR:begin
                      
                      aluop<= `EXE_OR_OP;
                      alusel<=`EXE_RES_R;
                      reg1_read_o<=1'b1;
                      reg2_read_o<=1'b1;
                      imm<=32'h0;              
                      wd<=inst_i[11:7];
                      end
                      
                     `EXE_AND:begin
                      aluop <= `EXE_AND_OP;
                      alusel<=`EXE_RES_R;
                      reg1_read_o<=1'b1;
                      reg2_read_o<=1'b1;
                      imm<=32'h0;     
                      wd<=inst_i[11:7];
                      end
                      
                     `EXE_XOR:begin
                      aluop<= `EXE_XOR_OP;
                      alusel<=`EXE_RES_R;
                      reg1_read_o<=1'b1;
                      reg2_read_o<=1'b1;
                      imm<=32'h0;                
                      wd<=inst_i[11:7];
                      end
                      default:begin
                      end
                      endcase//op2
        end//EXE_R_OP
        
        `EXE_I_OP:  begin//I_TYPE
                    case(op2)
                    
                    `EXE_ANDI:begin
                    aluop <= `EXE_AND_OP;
                    alusel<= `EXE_RES_I;
                    reg1_read_o<=1'b1;
                    reg2_read_o<=1'b0;
                    if(inst_i[31]==1'b1)begin
                    imm<={20'hFFFFF,inst_i[31:20]};
                    end
                    else if(inst_i[31]==1'b0)begin
                    imm<={20'h00000,inst_i[31:20]};
                    end
                    else begin
                    end                   
                    wd<=inst_i[11:7];
                    end
                    
                    
                    `EXE_ORI:begin
                    aluop <= `EXE_OR_OP;
                    alusel<=`EXE_RES_I;
                    reg1_read_o<=1'b1;
                    reg2_read_o<=1'b0;
                    if(inst_i[31]==1'b1)begin
                    imm<={20'hFFFFF,inst_i[31:20]};
                    end
                    else if(inst_i[31]==1'b0)begin
                    imm<={20'h00000,inst_i[31:20]};
                    end
                    else begin
                    end                   
                    wd<=inst_i[11:7];
                    end
                    
                    
                    `EXE_ADDI:begin
                    aluop <= `EXE_ADD_OP;
                    alusel<=`EXE_RES_I ;
                    reg1_read_o<=1'b1;
                    reg2_read_o<=1'b0;
                    if(inst_i[31]==1'b1)begin
                    imm<={20'hFFFFF,inst_i[31:20]};
                    end
                    else if(inst_i[31]==1'b0)begin
                    imm<={20'h00000,inst_i[31:20]};
                    end
                    else begin
                    end                   
                    wd<=inst_i[11:7];
                    end
                    
                    
                    `EXE_XORI:begin
                    aluop <= `EXE_XOR_OP;
                    alusel<=`EXE_RES_I;
                    reg1_read_o<=1'b1;
                    reg2_read_o<=1'b0;
                    if(inst_i[31]==1'b1)begin
                    imm<={20'hFFFFF,inst_i[31:20]};
                    end
                    else if(inst_i[31]==1'b0)begin
                    imm<={20'h00000,inst_i[31:20]};
                    end
                    else begin
                    end                   
                    wd<=inst_i[11:7];
                    end
                    default:begin
                    end
                    endcase//op2
         
        end//EXE_I_OP
        
        `EXE_B_OP:begin//B_TYPE
                    case(op2)
                    
                    `EXE_BEQ:begin
                    aluop <= `EXE_BEQ_OP;
                    reg1_read_o<=1'b1;
                    reg2_read_o<=1'b1;
                    if(inst_i[31]==1'b1)begin
                        imm<={20'hFFFFF,inst_i[7],inst_i[30:25],inst_i[11:8],1'b0};
                    end
                    else if(inst_i[31]==1'b0)begin
                        imm<={20'h00000,inst_i[7],inst_i[30:25],inst_i[11:8],1'b0};
                    end
                        else begin
                    end                
                    if(reg1==reg2)begin
                        alusel<=`EXE_RES_B;
                    end
                    else begin
                         alusel<=`EXE_RES_NB;
                    end
                    wd<=`NOPRegAddr;
                    end
                    
                    `EXE_BNE:begin
                    aluop <= `EXE_BNE_OP;
                    reg1_read_o<=1'b1;
                    reg2_read_o<=1'b1;
                    if(inst_i[31]==1'b1)begin
                        imm<={20'hFFFFF,inst_i[7],inst_i[30:25],inst_i[11:8],1'b0};
                    end
                    else if(inst_i[31]==1'b0)begin
                        imm<={20'h00000,inst_i[7],inst_i[30:25],inst_i[11:8],1'b0};
                    end
                        else begin
                    end                
                    if(reg1!=reg2)begin
                        alusel<=`EXE_RES_B;
                    end
                    else begin
                         alusel<=`EXE_RES_NB;
                    end
                    wd<=`NOPRegAddr;
                    end
                    
                    `EXE_BLT:begin
                    aluop <= `EXE_BLT_OP;
                    reg1_read_o<=1'b1;
                    reg2_read_o<=1'b1;
                    if(inst_i[31]==1'b1)begin
                        imm<={20'hFFFFF,inst_i[7],inst_i[30:25],inst_i[11:8],1'b0};
                    end
                    else if(inst_i[31]==1'b0)begin
                        imm<={20'h00000,inst_i[7],inst_i[30:25],inst_i[11:8],1'b0};
                    end
                        else begin
                    end                
                    if(reg1<reg2)begin
                        alusel<=`EXE_RES_B;
                    end
                    else begin
                         alusel<=`EXE_RES_NB;
                    end
                    wd<=`NOPRegAddr;
                    end
                    
                    `EXE_BGE:begin
                    aluop <= `EXE_BGE_OP;
                    reg1_read_o<=1'b1;
                    reg2_read_o<=1'b1;
                    if(inst_i[31]==1'b1)begin
                        imm<={20'hFFFFF,inst_i[7],inst_i[30:25],inst_i[11:8],1'b0};
                    end
                    else if(inst_i[31]==1'b0)begin
                        imm<={20'h00000,inst_i[7],inst_i[30:25],inst_i[11:8],1'b0};
                    end
                        else begin
                    end                
                    if(reg1>=reg2)begin
                        alusel<=`EXE_RES_B;
                    end
                    else begin
                         alusel<=`EXE_RES_NB;
                    end
                    wd<=`NOPRegAddr;
                    end
                    
                    `EXE_BLTU:begin
                    aluop <= `EXE_BLTU_OP;
                    reg1_read_o<=1'b1;
                    reg2_read_o<=1'b1;
                    if(inst_i[31]==1'b1)begin
                        imm<={20'hFFFFF,inst_i[7],inst_i[30:25],inst_i[11:8],1'b0};
                    end
                    else if(inst_i[31]==1'b0)begin
                        imm<={20'h00000,inst_i[7],inst_i[30:25],inst_i[11:8],1'b0};
                    end
                        else begin
                    end                
                    if(reg1<reg2)begin
                        alusel<=`EXE_RES_B;
                    end
                    else begin
                         alusel<=`EXE_RES_NB;
                    end
                    wd<=`NOPRegAddr;
                    end
                    
                    `EXE_BGEU:begin
                    aluop <= `EXE_BGEU_OP;
                    reg1_read_o<=1'b1;
                    reg2_read_o<=1'b1;
                    if(inst_i[31]==1'b1)begin
                        imm<={20'hFFFFF,inst_i[7],inst_i[30:25],inst_i[11:8],1'b0};
                    end
                    else if(inst_i[31]==1'b0)begin
                        imm<={20'h00000,inst_i[7],inst_i[30:25],inst_i[11:8],1'b0};
                    end
                        else begin
                    end                
                    if(reg1>=reg2)begin
                        alusel<=`EXE_RES_B;
                    end
                    else begin
                         alusel<=`EXE_RES_NB;
                    end
                    wd<=`NOPRegAddr;
                    end
                    
                    default:begin
                    end
                    endcase          
        end//EXE_B_OP
        
        `EXE_LW_OP:begin//I_TYPE_INSTR
         aluop <= `EXE_LW_OP;
         alusel<=`EXE_RES_LW;
         reg1_read_o<=1'b1;
         reg2_read_o<=1'b0;
         if(inst_i[31]==1'b1)begin      
         imm<={20'hFFFFF,inst_i[31:20]};
         end                            
         else if(inst_i[31]==1'b0)begin 
         imm<={20'h00000,inst_i[31:20]};
         end                            
         else begin                     
         end                            
         wd<=inst_i[11:7];
         end//EXE_LW_OP
        
        `EXE_SW_OP:begin
         aluop <= `EXE_SW_OP;
         alusel<=`EXE_RES_SW;
         reg1_read_o<=1'b1;
         reg2_read_o<=1'b1;
         if(inst_i[31]==1'b1)begin      
         imm<={20'hFFFFF,inst_i[31:25],inst_i[11:7]};
         end                            
         else if(inst_i[31]==1'b0)begin 
         imm<={20'h00000,inst_i[31:25],inst_i[11:7]};
         end                            
         else begin                     
         end                                     
         end//EXE_SW_OP
        
        `EXE_JAL_OP:begin
         
         aluop <= `EXE_JAL_OP;
         alusel<=`EXE_RES_JAL;
         reg1_read_o<=1'b0;
         reg2_read_o<=1'b0;
         if(inst_i[31]==1'b1)begin      
         imm<={12'hFFF,inst_i[19:12],inst_i[20],inst_i[30:21],1'b0};
         end                            
         else if(inst_i[31]==1'b0)begin 
         imm<={12'h000,inst_i[19:12],inst_i[20],inst_i[30:21],1'b0};
         end                            
         else begin                     
         end              
         wd<=inst_i[11:7];
         
        end//EXE_JAL_OP
        
        `EXE_JALR_OP :begin
         
         aluop <= `EXE_JALR_OP;
         alusel<=`EXE_RES_JALR;
         reg1_read_o<=1'b1;
         reg2_read_o<=1'b0; 
         if(inst_i[31]==1'b1)begin
         imm<={20'hFFFFF,inst_i[31:20]};
         end
         else if(inst_i[31]==1'b0)begin
         imm<={20'h00000,inst_i[31:20]};
         end
         else begin
         end                   
         wd<=inst_i[11:7];
        end//EXE_JALR_OP 
        
        default:begin
        end
    endcase//op1    
   end//else     
end//always       
        

always@(*)begin
    if(rst ==`RstEnable)begin
        reg1<=`ZeroWord;
    end
    else if(reg1_read_o==1'b1)begin
        reg1<=reg1_data_i;
    end
    else if(reg1_read_o==1'b0)begin
        reg1<=imm;
    end
    else begin
        reg1<=`ZeroWord;
    end
end    

always@(*)begin
    if(rst ==`RstEnable)begin
        reg2<=`ZeroWord;
    end
    else if(reg2_read_o==1'b1)begin
        reg2<=reg2_data_i;
    end
    else if(reg2_read_o==1'b0)begin
        reg2<=imm;
    end
    else begin
        reg2<=`ZeroWord;
    end
end    
always@(posedge id_en or posedge rst)begin
    if(rst==`RstEnable)begin
        aluop_o <= `EXE_NOP_OP  ;
        alusel_o <= `EXE_RES_NOP;
        wd_o <= `NOPRegAddr;
        reg1_o<=`ZeroWord;
        reg2_o<=`ZeroWord;
        imm_o<=32'h0;
    end
    else begin
        aluop_o <= aluop;
        alusel_o <=alusel;
        wd_o <= wd;
        reg1_o<=reg1;
        reg2_o<=reg2;
        imm_o<=imm;
    end
end
endmodule
*/

/* Code of regfile:
// global define
`define RstEnable 1'b1
`define RstDisable 1'b0
`define WriteEnable 1'b1
`define WriteDisable 1'b0
`define ReadEnable 1'b1
`define ReadDisable 1'b0
`define AluOpBus    6:0 //the width of translation aluop_o
`define AluSelBus   2:0 //the width of translation alusel_o
`define InstValid   1'b0 //vaild operator
`define InstInvalid 1'b1 //invaild operator
`define True_v      1'b1//meaning true
`define False_v     1'b0//meaning false
`define ChipDisable 1'b0//chip enable
`define ChipEnable  1'b1//chip ban

//opcode
`define EXE_R_OP          7'b0110011//R type opcode
`define EXE_I_OP          7'b0010011//I type opcode
`define EXE_B_OP          7'b1100011//B type opcode

//special 4 instructions opcode
`define EXE_LW        7'b0000011
`define EXE_SW        7'b0100011
`define EXE_JAL       7'b1101111
`define EXE_JALR      7'b1100111

//func3
`define EXE_OR            3'b110
`define EXE_AND           3'b111
`define EXE_ORI           3'b110
`define EXE_ADDI          3'b000
`define EXE_ANDI          3'b111
`define EXE_BEQ           3'b000
`define EXE_BNE           3'b001 
`define EXE_BLT           3'b100
`define EXE_BGE           3'b101
`define EXE_BLTU          3'b110
`define EXE_BGEU          3'b111
`define EXE_XOR           3'b100
`define EXE_XORI          3'b100

// func7
`define EXE_ADD           7'b0000000 
`define EXE_SUB           7'b0100000

//AluSel
`define EXE_RES_NOP                      7'b0000000
`define EXE_RES_R                        7'b0000101
`define EXE_RES_I                        7'b0100101
`define EXE_RES_LW                       7'b0101001
`define EXE_RES_SW                       7'b0111001
`define EXE_RES_B                        7'b1100010
`define EXE_RES_NB                       7'b0000000
`define EXE_RES_JAL                      7'b1100011
`define EXE_RES_JALR                     7'b1100111

//Aluop
//`define EXE_OR_OP 
//`define EXE_ADD_OP 
`define EXE_NOP_OP        3'b000//0
`define EXE_OR_OP         3'b001//1
`define EXE_AND_OP        3'b010//2
`define EXE_XOR_OP        3'b011//3
                          
`define EXE_ADD_OP        3'b100//4
`define EXE_SUB_OP        3'b101//5
                          
`define EXE_LW_OP         3'b101//4
`define EXE_SW_OP         3'b101//4
                          
`define EXE_BEQ_OP        3'b101//4
`define EXE_BNE_OP        3'b101//4
`define EXE_BLT_OP        3'b101//4
`define EXE_BGE_OP        3'b101//4
`define EXE_BLTU_OP       3'b101//4
`define EXE_BGEU_OP       3'b101//4
                          
`define EXE_JAL_OP        3'b101//4
`define EXE_JALR_OP       3'b101//4

//transer define
`define Branch      1'b1//transer 
`define NotBranch   1'b0//not transfer

//instruction memory about rom
`define ZeroWord    32'h00000000
`define InstAddrBus 31:0  //address
`define InstBus     31:0 //Data
`define InstMemNum  131071 //rom fact size 128K
`define InstMemNumLog2 17     //the real width of rom


//************************ reg total define
`define RegAddrBus  4:0   //regfile addr width
`define RegBus      31:0  //regfile data width
`define RegWidth    32    //in common use reg width
`define DoubleRegwidth 64 // double reg width
`define DoubleRegBus  63:0 //double data width
`define RegNum        32 //the num of reg
`define RegNumLog2    5 //the num of common reg
`define NOPRegAddr    5'b00000

module regfile (
    input wire                  clk,
    input wire                  rst,

    input wire                  we,
    input wire[`RegAddrBus]     waddr,
    input wire[`RegBus]         wdata,

    input wire                  re1,
    input wire[`RegAddrBus]     raddr1,
    output reg[`RegBus]         rdata1,

    input wire                  re2,
    input wire[`RegAddrBus]     raddr2,
    output reg[`RegBus]         rdata2


);

    reg[`RegBus] regs[0:`RegNum-1];

    always @ (posedge clk) begin
        if (rst == `RstDisable) begin
            if (we == `WriteEnable && waddr != `NOPRegAddr) begin
                regs[waddr] <= wdata;
            end
        end
    end

    always @ (*) begin
        if (rst == `RstEnable) begin
            rdata1 <= `ZeroWord;
        end else if (re1 == `ReadEnable) begin
            if (raddr1 == waddr && we == `WriteEnable) begin
                rdata1 <= wdata;
            end else if (raddr1 == `NOPRegAddr) begin
                rdata1 <= `ZeroWord;
            end else begin
                rdata1 <= regs[raddr1];
            end
        end else begin
            rdata1 <= `ZeroWord;
        end
    end

    always @ (*) begin
        if (rst == `RstEnable) begin
            rdata2 <= `ZeroWord;
        end else if (re2 == `ReadEnable) begin
            if (raddr2 == waddr && we == `WriteEnable) begin
                rdata2 <= wdata;
            end else if (raddr2 == `ZeroWord) begin
                rdata2 <= `ZeroWord;
            end else begin
                rdata2 <= regs[raddr2];
            end
        end else begin
            rdata2 <= `ZeroWord;
        end
    end
    
    always @(negedge we) begin
        $display("x3: %d, x4: %d", regs[3], regs[4]);
    end 

    
endmodule
*/
