// Digital circuit CU.dig as structural Verilog
module CU (
  input  clk,
  input  [6:0] alusel,
  output [1:0] out_3
);

  wire button_1_out, u_Control_Uint_ex_en, u_Control_Uint_id_en, u_Control_Uint_imm_en,
       u_Control_Uint_jump_en, u_Control_Uint_l_or_s, u_Control_Uint_mem_en, u_Control_Uint_pc_en,
       u_Control_Uint_wb_en;

  Button #(.activeLow("true")) button_1 (.out(button_1_out));
  Control_Uint #(.applicationType("IVERILOG"), .CodeFile("/home/weezz/CPU/design/Control_Unit.v")) u_Control_Uint (
    .clk(clk), .rst(button_1_out), .ALUSEL(alusel), .PC_en(u_Control_Uint_pc_en),
    .ID_en(u_Control_Uint_id_en), .EX_en(u_Control_Uint_ex_en), .MEM_en(u_Control_Uint_mem_en),
    .WB_en(u_Control_Uint_wb_en), .Jump_en(u_Control_Uint_jump_en), .imm_en(u_Control_Uint_imm_en),
    .L_or_S(u_Control_Uint_l_or_s), .WB_Ctrl(out_3));
  LED led_1 (.in(u_Control_Uint_pc_en));
  LED led_2 (.in(u_Control_Uint_id_en));
  LED led_3 (.in(u_Control_Uint_ex_en));
  LED led_4 (.in(u_Control_Uint_mem_en));
  LED led_5 (.in(u_Control_Uint_wb_en));
  LED led_6 (.in(u_Control_Uint_jump_en));
  LED led_7 (.in(u_Control_Uint_imm_en));
  LED led_8 (.in(u_Control_Uint_l_or_s));
endmodule
