// Digital circuit WB.dig as structural Verilog
module WB (
  input  [31:0] ram_data,
  input  [31:0] pc_plus_4,
  input  [31:0] ex_data,
  input  [1:0] ctrl,
  output [31:0] wb_data
);

  WB #(.applicationType("IVERILOG"), .CodeFile("/home/weezz/CPU/design/WB.v")) u_WB (
    .RAM_Data(ram_data), .PC_Plus4(pc_plus_4), .EX_Data(ex_data), .WB_Ctrl(ctrl), .WB_Data(wb_data));
endmodule
